// Logisim project branch_comp.circ as structural Verilog: 1 circuit, main circuit branch_comp
module branch_comp (
  input  [31:0] rs1,
  input  [31:0] rs2,
  input  BrUn,
  output BrEq,
  output BrLt
);

  wire Signed_Eq, Signed_Lt, Unsigned_Eq, Unsigned_Lt;

  Comparator #(.width(32)) comparator_1 (.a(rs1), .b(rs2), .eq(Signed_Eq), .lt(Signed_Lt));  // open: gt
  Comparator #(.mode("unsigned"), .width(32)) comparator_2 (
    .a(rs1), .b(rs2), .eq(Unsigned_Eq), .lt(Unsigned_Lt));  // open: gt
  Multiplexer #(.enable("false")) multiplexer_1 (.in0(Signed_Eq), .in1(Unsigned_Eq), .out(BrEq), .sel(BrUn));
  Multiplexer #(.enable("false")) multiplexer_2 (.in0(Signed_Lt), .in1(Unsigned_Lt), .out(BrLt), .sel(BrUn));

  // Notes on the sheet:
  //   INPUTS to your circuit
  //   DON'T CHANGE THE LOCATIONS OF THE INPUTS AND OUTPUTS!
  //   OUTPUT from your circuit
endmodule
