// Logisim project control_logic.circ as structural Verilog: 7 circuits, main circuit control_logic
module control_logic (
  input  [31:0] inst,
  input  BrEq,
  input  BrLt,
  output PCSel,
  output RegWEn,
  output [2:0] ImmSel,
  output BrUn,
  output ASel,
  output BSel,
  output [3:0] ALUSel,
  output MemRW,
  output [1:0] WBSel,
  output CSRSel,
  output CSRWen
);

  wire is_I_type, is_op_0x03, is_op_0x6f, is_op_0x13, is_op_0x17, is_op_0x23, is_op_0x33, is_op_0x37,
       is_op_0x63, is_op_0x67, is_op_0x73, is_U_type, not_1_out, not_2_out, not_3_out, not_4_out, not_5_out,
       not_6_out, not_7_out, not_8_out, not_9_out, not_10_out, not_11_out, not_12_out, not_13_out,
       not_14_out, not_15_out, not_16_out, not_17_out, not_18_out, not_19_out, not_20_out, not_21_out,
       not_22_out, not_23_out, not_24_out, not_25_out, not_26_out, not_27_out, not_28_out, not_29_out,
       or_3_out;
  wire [2:0] priority_encoder_1_out;
  wire [16:0] I_type_out, multiplexer_1_out, R_type_out, S_type_out, SB_type_out, U_type_out, UJ_type_out;

  not not_1 (not_1_out, inst[3]);
  not not_2 (not_2_out, inst[4]);
  not not_3 (not_3_out, inst[5]);
  not not_4 (not_4_out, inst[3]);
  not not_5 (not_5_out, inst[2]);
  not not_6 (not_6_out, inst[3]);
  not not_7 (not_7_out, inst[6]);
  not not_8 (not_8_out, inst[2]);
  not not_9 (not_9_out, inst[3]);
  not not_10 (not_10_out, inst[3]);
  not not_11 (not_11_out, inst[5]);
  not not_12 (not_12_out, inst[6]);
  not not_13 (not_13_out, inst[2]);
  and and_1 (is_op_0x03, inst[0], inst[1], not_13_out, not_1_out, not_2_out, not_3_out, not_14_out);
  not not_14 (not_14_out, inst[6]);
  and and_2 (is_op_0x67, inst[0], inst[1], inst[2], not_4_out, not_15_out, inst[5], inst[6]);
  not not_15 (not_15_out, inst[4]);
  and and_3 (is_op_0x33, inst[0], inst[1], not_5_out, not_6_out, inst[4], inst[5], not_7_out);
  and and_4 (is_op_0x63, inst[0], inst[1], not_8_out, not_9_out, not_16_out, inst[5], inst[6]);
  not not_16 (not_16_out, inst[4]);
  and and_5 (is_op_0x17, inst[0], inst[1], inst[2], not_10_out, inst[4], not_11_out, not_12_out);
  or or_1 (is_I_type, is_op_0x03, is_op_0x13, is_op_0x67, is_op_0x73);
  R_Type r_type_1 (
    .inst(inst), .BrEq(BrEq), .BrLt(BrLt), .PCSel(R_type_out[0]), .RegWEn(R_type_out[1]),
    .ImmSel(R_type_out[4:2]), .BrUn(R_type_out[5]), .ASel(R_type_out[6]), .BSel(R_type_out[7]),
    .ALUSel(R_type_out[11:8]), .MemRW(R_type_out[12]), .WBSel(R_type_out[14:13]), .CSRSel(R_type_out[15]),
    .CSRWen(R_type_out[16]));
  S_Type s_type_1 (
    .inst(inst), .BrEq(BrEq), .BrLt(BrLt), .PCSel(S_type_out[0]), .RegWEn(S_type_out[1]),
    .ImmSel(S_type_out[4:2]), .BrUn(S_type_out[5]), .ASel(S_type_out[6]), .BSel(S_type_out[7]),
    .ALUSel(S_type_out[11:8]), .MemRW(S_type_out[12]), .WBSel(S_type_out[14:13]), .CSRSel(S_type_out[15]),
    .CSRWen(S_type_out[16]));
  U_Type u_type_1 (
    .inst(inst), .BrEq(BrEq), .BrLt(BrLt), .PCSel(U_type_out[0]), .RegWEn(U_type_out[1]),
    .ImmSel(U_type_out[4:2]), .BrUn(U_type_out[5]), .ASel(U_type_out[6]), .BSel(U_type_out[7]),
    .ALUSel(U_type_out[11:8]), .MemRW(U_type_out[12]), .WBSel(U_type_out[14:13]), .CSRSel(U_type_out[15]),
    .CSRWen(U_type_out[16]));
  Priority_Encoder priority_encoder_1 (
    .in0(is_op_0x33), .in1(is_I_type), .in2(is_op_0x23), .in3(is_op_0x63), .in4(is_U_type), .in5(is_op_0x6f),
    .out(priority_encoder_1_out), .en_in(1'b1));  // open: in6, in7, gs, en_out
  not not_17 (not_17_out, inst[3]);
  not not_18 (not_18_out, inst[3]);
  not not_19 (not_19_out, inst[3]);
  Multiplexer #(.enable("false"), .select(3), .width(17)) multiplexer_1 (
    .in0(R_type_out), .in1(I_type_out), .in2(S_type_out), .in3(SB_type_out), .in4(U_type_out),
    .in5(UJ_type_out), .out(multiplexer_1_out), .sel(priority_encoder_1_out));  // open: in6, in7
  not not_20 (not_20_out, inst[2]);
  not not_21 (not_21_out, inst[5]);
  not not_22 (not_22_out, inst[6]);
  not not_23 (not_23_out, inst[2]);
  not not_24 (not_24_out, inst[2]);
  not not_25 (not_25_out, inst[4]);
  not not_26 (not_26_out, inst[6]);
  not not_27 (not_27_out, inst[4]);
  not not_28 (not_28_out, inst[3]);
  not not_29 (not_29_out, inst[6]);
  or or_2 (is_U_type, is_op_0x17, is_op_0x37);
  and and_6 (is_op_0x13, inst[0], inst[1], not_20_out, not_17_out, inst[4], not_21_out, not_22_out);
  and and_7 (is_op_0x73, inst[0], inst[1], not_23_out, not_18_out, inst[4], inst[5], inst[6]);
  and and_8 (is_op_0x23, inst[0], inst[1], not_24_out, not_19_out, not_25_out, inst[5], not_26_out);
  and and_9 (is_op_0x6f, inst[0], inst[1], inst[2], inst[3], not_27_out, inst[5], inst[6]);
  and and_10 (is_op_0x37, inst[0], inst[1], inst[2], not_28_out, inst[4], inst[5], not_29_out);
  Multiplexer #(.enable("false"), .width(17)) multiplexer_2 (
    .in0({17{1'b0}}), .in1(multiplexer_1_out),
    .out({CSRWen, CSRSel, WBSel, MemRW, ALUSel, BSel, ASel, BrUn, ImmSel, RegWEn, PCSel}), .sel(or_3_out));
  or or_3 (or_3_out, is_op_0x33, is_I_type, is_op_0x23, is_op_0x63, is_U_type, is_op_0x6f);
  I_Type i_type_1 (
    .inst(inst), .BrEq(BrEq), .BrLt(BrLt), .PCSel(I_type_out[0]), .RegWEn(I_type_out[1]),
    .ImmSel(I_type_out[4:2]), .BrUn(I_type_out[5]), .ASel(I_type_out[6]), .BSel(I_type_out[7]),
    .ALUSel(I_type_out[11:8]), .MemRW(I_type_out[12]), .WBSel(I_type_out[14:13]), .CSRSel(I_type_out[15]),
    .CSRWen(I_type_out[16]));
  SB_Type sb_type_1 (
    .inst(inst), .BrEq(BrEq), .BrLt(BrLt), .PCSel(SB_type_out[0]), .RegWEn(SB_type_out[1]),
    .ImmSel(SB_type_out[4:2]), .BrUn(SB_type_out[5]), .ASel(SB_type_out[6]), .BSel(SB_type_out[7]),
    .ALUSel(SB_type_out[11:8]), .MemRW(SB_type_out[12]), .WBSel(SB_type_out[14:13]),
    .CSRSel(SB_type_out[15]), .CSRWen(SB_type_out[16]));
  UJ_Type uj_type_1 (
    .inst(inst), .BrEq(BrEq), .BrLt(BrLt), .PCSel(UJ_type_out[0]), .RegWEn(UJ_type_out[1]),
    .ImmSel(UJ_type_out[4:2]), .BrUn(UJ_type_out[5]), .ASel(UJ_type_out[6]), .BSel(UJ_type_out[7]),
    .ALUSel(UJ_type_out[11:8]), .MemRW(UJ_type_out[12]), .WBSel(UJ_type_out[14:13]),
    .CSRSel(UJ_type_out[15]), .CSRWen(UJ_type_out[16]));

  // Other names for the same wires on the sheet: opcode[6:0] = inst[6:0]; funct3[2:0] = inst[14:12];
  //   funct7[6:0] = inst[31:25]; is_UJ_type = is_op_0x6f; is_S_type = is_op_0x23; is_R_type = is_op_0x33;
  //   is_SB_type = is_op_0x63

  // Notes on the sheet:
  //   INPUTS to your circuit
  //   DON'T CHANGE THE LOCATIONS OF THE INPUTS AND OUTPUTS!
  //   OUTPUT from your circuit
endmodule

module R_Type (
  input  [31:0] inst,
  input  BrEq,
  input  BrLt,
  output PCSel,
  output RegWEn,
  output [2:0] ImmSel,
  output BrUn,
  output ASel,
  output BSel,
  output [3:0] ALUSel,
  output MemRW,
  output [1:0] WBSel,
  output CSRSel,
  output CSRWen
);

  wire is_add, is_and, is_f3_0x0, is_f3_0x1, is_f3_0x2, is_f3_0x3, is_f3_0x4, is_f3_0x5, is_f3_0x6,
       is_f3_0x7, is_f7_0x00, is_f7_0x01, is_f7_0x20, is_mul, is_mulh, is_mulhu, is_op_0x33, is_or, is_sll,
       is_slt, is_sra, is_srl, is_sub, is_xor, not_1_out, not_2_out, not_3_out, not_4_out, not_5_out,
       not_6_out, not_7_out, not_8_out, not_9_out, not_10_out, not_11_out, not_12_out, not_13_out,
       not_14_out, not_15_out, not_16_out, not_17_out, not_18_out, not_19_out, not_20_out, not_21_out,
       not_22_out, not_23_out, not_24_out, not_25_out, not_26_out, not_27_out, not_28_out, not_29_out,
       not_30_out, not_31_out, not_32_out, not_33_out, not_34_out;
  wire [3:0] priority_encoder_1_out;

  not not_1 (not_1_out, inst[12]);
  not not_2 (not_2_out, inst[13]);
  not not_3 (not_3_out, inst[14]);
  not not_4 (not_4_out, inst[13]);
  not not_5 (not_5_out, inst[14]);
  not not_6 (not_6_out, inst[12]);
  not not_7 (not_7_out, inst[14]);
  not not_8 (not_8_out, inst[14]);
  not not_9 (not_9_out, inst[12]);
  not not_10 (not_10_out, inst[13]);
  not not_11 (not_11_out, inst[13]);
  not not_12 (not_12_out, inst[12]);
  and and_1 (is_add, is_op_0x33, is_f3_0x0, is_f7_0x00);
  and and_2 (is_sll, is_op_0x33, is_f3_0x1, is_f7_0x00);
  and and_3 (is_slt, is_op_0x33, is_f3_0x2, is_f7_0x00);
  and and_4 (is_sra, is_op_0x33, is_f3_0x5, is_f7_0x20);
  and and_5 (is_f3_0x0, not_1_out, not_2_out, not_3_out);
  and and_6 (is_f3_0x1, inst[12], not_4_out, not_5_out);
  and and_7 (is_f3_0x2, not_6_out, inst[13], not_7_out);
  and and_8 (is_f3_0x3, inst[12], inst[13], not_8_out);
  and and_9 (is_f3_0x4, not_9_out, not_10_out, inst[14]);
  and and_10 (is_f3_0x5, inst[12], not_11_out, inst[14]);
  and and_11 (is_f3_0x6, not_12_out, inst[13], inst[14]);
  and and_12 (is_f3_0x7, inst[12], inst[13], inst[14]);
  not not_13 (not_13_out, inst[3]);
  not not_14 (not_14_out, inst[6]);
  not not_15 (not_15_out, inst[2]);
  and and_13 (is_op_0x33, inst[0], inst[1], not_15_out, not_13_out, inst[4], inst[5], not_14_out);
  not not_16 (not_16_out, inst[25]);
  not not_17 (not_17_out, inst[26]);
  not not_18 (not_18_out, inst[30]);
  not not_19 (not_19_out, inst[26]);
  not not_20 (not_20_out, inst[30]);
  not not_21 (not_21_out, inst[25]);
  not not_22 (not_22_out, inst[26]);
  and and_14 (is_mul, is_op_0x33, is_f3_0x0, is_f7_0x01);
  and and_15 (is_mulh, is_op_0x33, is_f3_0x1, is_f7_0x01);
  and and_16 (is_xor, is_op_0x33, is_f3_0x4, is_f7_0x00);
  and and_17 (is_or, is_op_0x33, is_f3_0x6, is_f7_0x00);
  not not_23 (not_23_out, inst[27]);
  not not_24 (not_24_out, inst[28]);
  not not_25 (not_25_out, inst[29]);
  not not_26 (not_26_out, inst[31]);
  not not_27 (not_27_out, inst[27]);
  not not_28 (not_28_out, inst[28]);
  not not_29 (not_29_out, inst[29]);
  not not_30 (not_30_out, inst[31]);
  not not_31 (not_31_out, inst[27]);
  not not_32 (not_32_out, inst[28]);
  not not_33 (not_33_out, inst[29]);
  not not_34 (not_34_out, inst[31]);
  and and_18 (is_f7_0x00, not_16_out, not_17_out, not_23_out, not_24_out, not_25_out, not_18_out, not_26_out);
  and and_19 (is_f7_0x01, inst[25], not_19_out, not_27_out, not_28_out, not_29_out, not_20_out, not_30_out);
  and and_20 (is_f7_0x20, not_21_out, not_22_out, not_31_out, not_32_out, not_33_out, inst[30], not_34_out);
  Priority_Encoder #(.select(4)) priority_encoder_1 (
    .in0(is_add), .in1(is_and), .in2(is_or), .in3(is_xor), .in4(is_srl), .in5(is_sra), .in6(is_sll),
    .in7(is_slt), .in10(is_mul), .in11(is_mulhu), .in12(is_sub), .in14(is_mulh),
    .out(priority_encoder_1_out), .en_in(1'b1));  // open: in8, in9, in13, in15, gs, en_out
  and and_21 (is_sub, is_op_0x33, is_f3_0x0, is_f7_0x20);
  and and_22 (is_mulhu, is_op_0x33, is_f3_0x3, is_f7_0x01);
  and and_23 (is_srl, is_op_0x33, is_f3_0x5, is_f7_0x00);
  and and_24 (is_and, is_op_0x33, is_f3_0x7, is_f7_0x00);
  Multiplexer #(.enable("false"), .select(4), .width(4)) multiplexer_1 (
    .in0(4'b0000), .in1(4'b0001), .in2(4'b0010), .in3(4'b0011), .in4(4'b0100), .in5(4'b0101), .in6(4'b0110),
    .in7(4'b0111), .in8(4'b1000), .in9(4'b1001), .in10(4'b1010), .in11(4'b1011), .in12(4'b1100),
    .in13(4'b1101), .in14(4'b1110), .in15(4'b1111), .out(ALUSel), .sel(priority_encoder_1_out));

  assign ASel = 1'b0;
  assign BSel = 1'b0;
  assign MemRW = 1'b0;
  assign PCSel = 1'b0;
  assign RegWEn = 1'b1;
  assign WBSel = 2'b01;

  // Other names for the same wires on the sheet: opcode[6:0] = inst[6:0]; funct3[2:0] = inst[14:12];
  //   funct7[6:0] = inst[31:25]

  // Notes on the sheet:
  //   INPUTS to your circuit
  //   DON'T CHANGE THE LOCATIONS OF THE INPUTS AND OUTPUTS!
  //   OUTPUT from your circuit
endmodule

module I_Type (
  input  [31:0] inst,
  input  BrEq,
  input  BrLt,
  output PCSel,
  output RegWEn,
  output [2:0] ImmSel,
  output BrUn,
  output ASel,
  output BSel,
  output [3:0] ALUSel,
  output MemRW,
  output [1:0] WBSel,
  output CSRSel,
  output CSRWen
);

  wire is_addi, is_andi, is_csrw, is_f3_0x0, is_f3_0x1, is_f3_0x2, is_f3_0x3, is_f3_0x4, is_f3_0x5,
       is_f3_0x6, is_f3_0x7, is_f7_0x00, is_f7_0x01, is_f7_0x20, is_lb, is_lh, is_lw, is_op_0x03, is_op_0x13,
       is_op_0x67, is_op_0x73, is_ori, is_slli, is_slti, is_srai, is_srli, is_xori, not_1_out, not_2_out,
       not_3_out, not_4_out, not_5_out, not_6_out, not_7_out, not_8_out, not_9_out, not_10_out, not_11_out,
       not_12_out, not_13_out, not_14_out, not_15_out, not_16_out, not_17_out, not_18_out, not_19_out,
       not_20_out, not_21_out, not_22_out, not_23_out, not_24_out, not_25_out, not_26_out, not_27_out,
       not_28_out, not_29_out, not_30_out, not_31_out, not_32_out, not_33_out, not_34_out, not_35_out,
       not_36_out, not_37_out, not_38_out, not_39_out, not_40_out, not_41_out, not_42_out, not_43_out,
       not_44_out, or_1_out, or_2_out;
  wire [1:0] priority_encoder_2_out;
  wire [3:0] priority_encoder_1_out;

  not not_1 (not_1_out, inst[12]);
  not not_2 (not_2_out, inst[13]);
  not not_3 (not_3_out, inst[14]);
  not not_4 (not_4_out, inst[13]);
  not not_5 (not_5_out, inst[14]);
  not not_6 (not_6_out, inst[12]);
  not not_7 (not_7_out, inst[14]);
  not not_8 (not_8_out, inst[14]);
  and and_1 (is_lb, is_op_0x03, is_f3_0x0);
  and and_2 (is_lh, is_op_0x03, is_f3_0x1);
  and and_3 (is_lw, is_op_0x03, is_f3_0x2);
  and and_4 (is_addi, is_op_0x13, is_f3_0x0);
  and and_5 (is_slli, is_op_0x13, is_f3_0x1, is_f7_0x00);
  and and_6 (is_f3_0x0, not_1_out, not_2_out, not_3_out);
  and and_7 (is_f3_0x1, inst[12], not_4_out, not_5_out);
  and and_8 (is_f3_0x2, not_6_out, inst[13], not_7_out);
  and and_9 (is_f3_0x3, inst[12], inst[13], not_8_out);
  Priority_Encoder #(.select(4)) priority_encoder_1 (
    .in0(is_lb), .in1(is_lh), .in2(is_lw), .in3(is_addi), .in4(PCSel), .in5(is_csrw), .in6(CSRSel),
    .in7(is_andi), .in8(is_ori), .in9(is_xori), .in10(is_srli), .in11(is_srai), .in12(is_slli),
    .in13(is_slti), .out(priority_encoder_1_out), .en_in(1'b1));  // open: in14, in15, gs, en_out
  not not_9 (not_9_out, inst[2]);
  not not_10 (not_10_out, inst[3]);
  not not_11 (not_11_out, inst[4]);
  not not_12 (not_12_out, inst[5]);
  not not_13 (not_13_out, inst[6]);
  not not_14 (not_14_out, inst[3]);
  not not_15 (not_15_out, inst[4]);
  Multiplexer #(.enable("false"), .select(4), .width(4)) multiplexer_1 (
    .in0(4'b0000), .in1(4'b0000), .in2(4'b0000), .in3(4'b0000), .in4(4'b0000), .in5(4'b0000), .in6(4'b0000),
    .in7(4'b0001), .in8(4'b0010), .in9(4'b0011), .in10(4'b0100), .in11(4'b0101), .in12(4'b0110),
    .in13(4'b0111), .out(ALUSel), .sel(priority_encoder_1_out));  // open: in14, in15
  and and_10 (is_op_0x03, inst[0], inst[1], not_9_out, not_10_out, not_11_out, not_12_out, not_13_out);
  and and_11 (is_op_0x67, inst[0], inst[1], inst[2], not_14_out, not_15_out, inst[5], inst[6]);
  not not_16 (not_16_out, inst[12]);
  not not_17 (not_17_out, inst[13]);
  not not_18 (not_18_out, inst[13]);
  not not_19 (not_19_out, inst[12]);
  and and_12 (is_slti, is_op_0x13, is_f3_0x2);
  and and_13 (is_xori, is_op_0x13, is_f3_0x4);
  and and_14 (is_srli, is_op_0x13, is_f3_0x5, is_f7_0x00);
  and and_15 (is_srai, is_op_0x13, is_f3_0x5, is_f7_0x20);
  and and_16 (is_ori, is_op_0x13, is_f3_0x6);
  and and_17 (is_f3_0x4, not_16_out, not_17_out, inst[14]);
  and and_18 (is_f3_0x5, inst[12], not_18_out, inst[14]);
  and and_19 (is_f3_0x6, not_19_out, inst[13], inst[14]);
  and and_20 (is_f3_0x7, inst[12], inst[13], inst[14]);
  not not_20 (not_20_out, inst[3]);
  not not_21 (not_21_out, inst[6]);
  not not_22 (not_22_out, inst[3]);
  and and_21 (is_andi, is_op_0x13, is_f3_0x7);
  and and_22 (PCSel, is_op_0x67, is_f3_0x0);
  and and_23 (is_csrw, is_op_0x73, is_f3_0x1);
  and and_24 (CSRSel, is_op_0x73, is_f3_0x5);
  not not_23 (not_23_out, inst[2]);
  and and_25 (is_op_0x13, inst[0], inst[1], not_23_out, not_20_out, inst[4], not_24_out, not_21_out);
  not not_24 (not_24_out, inst[5]);
  not not_25 (not_25_out, inst[2]);
  and and_26 (is_op_0x73, inst[0], inst[1], not_25_out, not_22_out, inst[4], inst[5], inst[6]);
  Priority_Encoder #(.select(2)) priority_encoder_2 (
    .in0(PCSel), .in1(or_1_out), .in2(or_2_out), .out(priority_encoder_2_out), .en_in(1'b1));  // open: in3, gs, en_out
  or or_1 (or_1_out, is_addi, is_andi, is_ori, is_xori, is_srli, is_srai, is_slli, is_slti);
  or or_2 (or_2_out, is_lb, is_lh, is_lw);
  not not_26 (not_26_out, inst[25]);
  not not_27 (not_27_out, inst[26]);
  not not_28 (not_28_out, inst[30]);
  not not_29 (not_29_out, inst[26]);
  not not_30 (not_30_out, inst[30]);
  not not_31 (not_31_out, inst[25]);
  not not_32 (not_32_out, inst[26]);
  Multiplexer #(.enable("false"), .select(2), .width(2)) multiplexer_2 (
    .in0(2'b00), .in1(2'b01), .in2(2'b10), .out(WBSel), .sel(priority_encoder_2_out));  // open: in3
  not not_33 (not_33_out, inst[27]);
  not not_34 (not_34_out, inst[28]);
  not not_35 (not_35_out, inst[29]);
  not not_36 (not_36_out, inst[31]);
  not not_37 (not_37_out, inst[27]);
  not not_38 (not_38_out, inst[28]);
  not not_39 (not_39_out, inst[29]);
  not not_40 (not_40_out, inst[31]);
  not not_41 (not_41_out, inst[27]);
  not not_42 (not_42_out, inst[28]);
  not not_43 (not_43_out, inst[29]);
  not not_44 (not_44_out, inst[31]);
  and and_27 (is_f7_0x00, not_26_out, not_27_out, not_33_out, not_34_out, not_35_out, not_28_out, not_36_out);
  and and_28 (is_f7_0x01, inst[25], not_29_out, not_37_out, not_38_out, not_39_out, not_30_out, not_40_out);
  and and_29 (is_f7_0x20, not_31_out, not_32_out, not_41_out, not_42_out, not_43_out, inst[30], not_44_out);
  or or_3 (CSRWen, is_csrw, CSRSel);

  assign ASel = 1'b0;
  assign BSel = 1'b1;
  assign ImmSel = 3'b000;
  assign MemRW = 1'b0;
  assign RegWEn = 1'b1;

  // Other names for the same wires on the sheet: opcode[6:0] = inst[6:0]; funct3[2:0] = inst[14:12];
  //   funct7[6:0] = inst[31:25]; is_csrwi = CSRSel; is_jalr = PCSel

  // Notes on the sheet:
  //   INPUTS to your circuit
  //   I-imm
  //   DON'T CHANGE THE LOCATIONS OF THE INPUTS AND OUTPUTS!
  //   OUTPUT from your circuit
endmodule

module S_Type (
  input  [31:0] inst,
  input  BrEq,
  input  BrLt,
  output PCSel,
  output RegWEn,
  output [2:0] ImmSel,
  output BrUn,
  output ASel,
  output BSel,
  output [3:0] ALUSel,
  output MemRW,
  output [1:0] WBSel,
  output CSRSel,
  output CSRWen
);

  wire is_f3_0x0, is_f3_0x1, is_f3_0x2, is_op_0x23, not_1_out, not_2_out, not_3_out, not_4_out, not_5_out,
       not_6_out, not_7_out, not_8_out, not_9_out, not_10_out, not_11_out;

  not not_1 (not_1_out, inst[12]);
  not not_2 (not_2_out, inst[13]);
  not not_3 (not_3_out, inst[14]);
  and and_1 (is_f3_0x0, not_1_out, not_2_out, not_3_out);
  not not_4 (not_4_out, inst[3]);
  not not_5 (not_5_out, inst[6]);
  not not_6 (not_6_out, inst[2]);
  and and_2 (is_op_0x23, inst[0], inst[1], not_6_out, not_4_out, not_7_out, inst[5], not_5_out);
  not not_7 (not_7_out, inst[4]);
  not not_8 (not_8_out, inst[13]);
  not not_9 (not_9_out, inst[14]);
  and and_3 (is_f3_0x1, inst[12], not_8_out, not_9_out);
  not not_10 (not_10_out, inst[12]);
  not not_11 (not_11_out, inst[14]);
  and and_4 (is_f3_0x2, not_10_out, inst[13], not_11_out);

  assign ALUSel = 4'b0000;
  assign ASel = 1'b0;
  assign BSel = 1'b1;
  assign ImmSel = 3'b001;
  assign MemRW = 1'b1;
  assign PCSel = 1'b0;
  assign RegWEn = 1'b0;

  // Other names for the same wires on the sheet: opcode[6:0] = inst[6:0]; funct3[2:0] = inst[14:12];
  //   funct7[6:0] = inst[31:25]

  // Notes on the sheet:
  //   INPUTS to your circuit
  //   S-imm
  //   DON'T CHANGE THE LOCATIONS OF THE INPUTS AND OUTPUTS!
  //   OUTPUT from your circuit
endmodule

module SB_Type (
  input  [31:0] inst,
  input  BrEq,
  input  BrLt,
  output PCSel,
  output RegWEn,
  output [2:0] ImmSel,
  output BrUn,
  output ASel,
  output BSel,
  output [3:0] ALUSel,
  output MemRW,
  output [1:0] WBSel,
  output CSRSel,
  output CSRWen
);

  wire and_6_out, and_7_out, and_8_out, and_9_out, and_10_out, and_11_out, is_beq, is_bge, is_bgeu, is_blt,
       is_bltu, is_bne, is_f3_0x0, is_f3_0x1, is_f3_0x4, is_f3_0x5, is_f3_0x6, is_f3_0x7, is_op_0x63,
       not_1_out, not_2_out, not_3_out, not_4_out, not_5_out, not_6_out, not_7_out, not_8_out, not_9_out,
       not_10_out, not_11_out, not_12_out, not_13_out, not_14_out, not_15_out;

  not not_1 (not_1_out, inst[12]);
  not not_2 (not_2_out, inst[13]);
  not not_3 (not_3_out, inst[14]);
  not not_4 (not_4_out, inst[13]);
  not not_5 (not_5_out, inst[14]);
  not not_6 (not_6_out, inst[12]);
  not not_7 (not_7_out, inst[13]);
  not not_8 (not_8_out, BrEq);
  not not_9 (not_9_out, BrLt);
  not not_10 (not_10_out, BrLt);
  and and_1 (is_f3_0x0, not_1_out, not_2_out, not_3_out);
  and and_2 (is_f3_0x1, inst[12], not_4_out, not_5_out);
  and and_3 (is_f3_0x4, not_6_out, not_7_out, inst[14]);
  and and_4 (is_beq, is_op_0x63, is_f3_0x0);
  and and_5 (is_bne, is_op_0x63, is_f3_0x1);
  and and_6 (and_6_out, is_beq, BrEq);
  and and_7 (and_7_out, is_bne, not_8_out);
  and and_8 (and_8_out, is_blt, BrLt);
  and and_9 (and_9_out, is_bge, not_9_out);
  and and_10 (and_10_out, is_bltu, BrLt);
  and and_11 (and_11_out, is_bgeu, not_10_out);
  not not_11 (not_11_out, inst[3]);
  not not_12 (not_12_out, inst[2]);
  and and_12 (is_op_0x63, inst[0], inst[1], not_12_out, not_11_out, not_13_out, inst[5], inst[6]);
  not not_13 (not_13_out, inst[4]);
  not not_14 (not_14_out, inst[12]);
  not not_15 (not_15_out, inst[13]);
  and and_13 (is_f3_0x5, inst[12], not_15_out, inst[14]);
  and and_14 (is_f3_0x6, not_14_out, inst[13], inst[14]);
  and and_15 (is_f3_0x7, inst[12], inst[13], inst[14]);
  and and_16 (is_blt, is_op_0x63, is_f3_0x4);
  and and_17 (is_bge, is_op_0x63, is_f3_0x5);
  or or_1 (PCSel, and_6_out, and_7_out, and_8_out, and_9_out, and_10_out, and_11_out);
  and and_18 (is_bltu, is_op_0x63, is_f3_0x6);
  and and_19 (is_bgeu, is_op_0x63, is_f3_0x7);
  or or_2 (BrUn, is_bltu, is_bgeu);

  assign ALUSel = 4'b0000;
  assign ASel = 1'b1;
  assign BSel = 1'b1;
  assign ImmSel = 3'b010;
  assign MemRW = 1'b0;
  assign RegWEn = 1'b0;

  // Other names for the same wires on the sheet: opcode[6:0] = inst[6:0]; funct3[2:0] = inst[14:12];
  //   funct7[6:0] = inst[31:25]

  // Notes on the sheet:
  //   INPUTS to your circuit
  //   SB-imm
  //   DON'T CHANGE THE LOCATIONS OF THE INPUTS AND OUTPUTS!
  //   OUTPUT from your circuit
endmodule

module U_Type (
  input  [31:0] inst,
  input  BrEq,
  input  BrLt,
  output PCSel,
  output RegWEn,
  output [2:0] ImmSel,
  output BrUn,
  output ASel,
  output BSel,
  output [3:0] ALUSel,
  output MemRW,
  output [1:0] WBSel,
  output CSRSel,
  output CSRWen
);

  wire is_lui, not_1_out, not_2_out, not_3_out, not_4_out, not_5_out;

  not not_1 (not_1_out, inst[3]);
  not not_2 (not_2_out, inst[6]);
  and and_1 (ASel, inst[0], inst[1], inst[2], not_1_out, inst[4], not_3_out, not_2_out);
  not not_3 (not_3_out, inst[5]);
  not not_4 (not_4_out, inst[3]);
  not not_5 (not_5_out, inst[6]);
  and and_2 (is_lui, inst[0], inst[1], inst[2], not_4_out, inst[4], inst[5], not_5_out);

  assign ALUSel = 4'b0000;
  assign BSel = 1'b1;
  assign ImmSel = 3'b011;
  assign MemRW = 1'b0;
  assign PCSel = 1'b0;
  assign RegWEn = 1'b1;
  assign WBSel = 2'b01;

  // Other names for the same wires on the sheet: opcode[6:0] = inst[6:0]; funct3[2:0] = inst[14:12];
  //   funct7[6:0] = inst[31:25]; is_auipc = ASel; is_op_0x17 = ASel; is_op_0x37 = is_lui

  // Notes on the sheet:
  //   INPUTS to your circuit
  //   U-imm
  //   DON'T CHANGE THE LOCATIONS OF THE INPUTS AND OUTPUTS!
  //   OUTPUT from your circuit
endmodule

module UJ_Type (
  input  [31:0] inst,
  input  BrEq,
  input  BrLt,
  output PCSel,
  output RegWEn,
  output [2:0] ImmSel,
  output BrUn,
  output ASel,
  output BSel,
  output [3:0] ALUSel,
  output MemRW,
  output [1:0] WBSel,
  output CSRSel,
  output CSRWen
);

  wire is_op_0x6f, not_1_out;

  and and_1 (is_op_0x6f, inst[0], inst[1], inst[2], inst[3], not_1_out, inst[5], inst[6]);
  not not_1 (not_1_out, inst[4]);

  assign ALUSel = 4'b0000;
  assign ASel = 1'b1;
  assign BSel = 1'b1;
  assign ImmSel = 3'b100;
  assign MemRW = 1'b0;
  assign PCSel = 1'b1;
  assign RegWEn = 1'b1;
  assign WBSel = 2'b00;

  // Other names for the same wires on the sheet: opcode[6:0] = inst[6:0]; funct3[2:0] = inst[14:12];
  //   funct7[6:0] = inst[31:25]

  // Notes on the sheet:
  //   INPUTS to your circuit
  //   UJ-imm
  //   DON'T CHANGE THE LOCATIONS OF THE INPUTS AND OUTPUTS!
  //   OUTPUT from your circuit
endmodule
