// Logisim project imm_gen.circ as structural Verilog: 1 circuit, main circuit imm_gen
module imm_gen (
  input  [31:0] inst,
  input  [2:0] ImmSel,
  output [31:0] imm
);

  wire [31:0] I_imm, S_imm, SB_imm, UJ_imm;

  assign I_imm = {{20{inst[31]}}, inst[31:20]};  // Bit_Extender bit_extender_1
  assign SB_imm = {{19{inst[31]}}, {inst[31], inst[7], inst[30:25], inst[11:8], 1'b0}};  // Bit_Extender bit_extender_2
  assign UJ_imm = {{11{inst[31]}}, {inst[31], inst[19:12], inst[20], inst[30:21], 1'b0}};  // Bit_Extender bit_extender_3
  Multiplexer #(.enable("false"), .select(3), .width(32)) multiplexer_1 (
    .in0(I_imm), .in1(S_imm), .in2(SB_imm), .in3({inst[31:12], {12{1'b0}}}), .in4(UJ_imm), .out(imm),
    .sel(ImmSel));  // open: in5, in6, in7
  assign S_imm = {{20{inst[31]}}, {inst[31:25], inst[11:7]}};  // Bit_Extender bit_extender_4

  // Other names for the same wires on the sheet: inst7_11[4:0] = inst[11:7]; inst8_11[3:0] = inst[11:8];
  //   opcode_inst_0_6[6:0] = inst[6:0]; funct3_inst12_14[2:0] = inst[14:12]; U_imm[31:12] = inst[31:12];
  //   rs1_inst_15_19[4:0] = inst[19:15]; inst20_24[4:0] = inst[24:20]; inst21_24[3:0] = inst[24:21];
  //   inst25_30[5:0] = inst[30:25]; inst25_31[6:0] = inst[31:25]

  // Notes on the sheet:
  //   INPUTS to your circuit
  //   I-immediate
  //   SB-immediate
  //   UJ-immediate
  //   DON'T CHANGE THE LOCATIONS OF THE INPUTS AND OUTPUTS!
  //   S-immediate
  //   U-immediate
  //   Imm_Sel
  //   OUTPUT from your circuit
endmodule
